// Logisim project Ex1.circ as structural Verilog
module circuito02 (
  input  a,
  input  b,
  input  c,
  input  d,
  input  e,
  output out_6
);

  wire and_1_out, and_2_out, and_3_out, and_4_out, nand_1_out, not_1_out, not_2_out, not_3_out, or_1_out,
       or_2_out, or_3_out, undriven, xor_1_out;

  and and_1 (and_1_out, a, c, e);
  xor xor_1 (xor_1_out, b, undriven);
  not not_1 (not_1_out, undriven);
  not not_2 (not_2_out, and_1_out);
  and and_2 (and_2_out, not_1_out, c, a);
  or or_1 (or_1_out, not_2_out, xor_1_out);
  and and_3 (and_3_out, xor_1_out, d);
  and and_4 (and_4_out, or_1_out, and_3_out);
  nand nand_1 (nand_1_out, and_3_out, and_2_out);
  not not_3 (not_3_out, or_2_out);
  or or_2 (or_2_out, and_3_out, nand_1_out, e);
  or or_3 (or_3_out, and_4_out, not_3_out);
  not not_4 (out_6, or_3_out);
endmodule

module Circuito01 (
  input  in_1,
  input  in_2,
  input  in_3,
  input  in_4,
  output out_5
);

  wire and_1_out, and_2_out;

  and and_1 (and_1_out, in_1, in_2);
  and and_2 (and_2_out, in_3, in_4);
  or or_1 (out_5, and_1_out, and_2_out);
endmodule
